# Fritzing sketch NeoStrand (saved by Fritzing 0.9.3b)
circuit board: 4.55627cm x 4.33382cm

parts:
  ATMEL328 = Arduino Pro Mini (5V)
  AQUA = Pushbutton [package="[THT]"]
  GOLD = Pushbutton [package="[THT]"]
  PINK = Pushbutton [package="[THT]"]
  TRIM = POT [package=trim_pot]
  NEOPIXEL1 = Neopixel Strip -- White (60/m) [part_number=1138]
  R1 = Resistor [tolerance=±5% resistance=470 package="1206 [SMD]"]
  5VDC = 2.1mm Barrel Jack with Terminal Block
  C1 = Capacitor Polarized [package=cpol-radial-1000uf-63v]

nets:
  VCC: ATMEL328.VCC, NEOPIXEL1.+5V, 5VDC.POS, C1.+
  GND: ATMEL328.GND, AQUA.Pin_3, AQUA.Pin_4, GOLD.Pin_3, GOLD.Pin_4, PINK.Pin_3, PINK.Pin_4, NEOPIXEL1.GND, 5VDC.NEG, C1.-
  N1: ATMEL328.A2, TRIM.S
  N2: ATMEL328.A0, TRIM.A
  N3: ATMEL328.MOSI, R1.Pin_0
  N4: ATMEL328.D9, PINK.Pin_1, PINK.Pin_2
  N5: ATMEL328.D8, GOLD.Pin_1, GOLD.Pin_2
  N6: ATMEL328.D7, AQUA.Pin_1, AQUA.Pin_2
  N7: NEOPIXEL1.DI, R1.Pin_1

notes:
  This is a simple NeoPixel (WS8212b) Strand Controller.
  Code on the Arduino / ATMEL328 can use AdaFruit library or the alternative FastLED library. In addition, three input buttons are wired for INPUT_PULLUP mode, and a dimmer potentiometer to adjust brightness or pattern speed.
  Many projects can use this as a foundation. See Ed Halley's NeoStrand project for how to incorporate software that uses this setup in detail.
  Input power must be pre-regulated 5VDC, such as from a USB power brick, and able to provide enough current for NeoPixels. Estimate 2A for 100 pixels.
  470Ω
  10kΩ
  1000µF
  10V+
  5VDC (Pre-Regulated)
  sample part arrangement
  (lays flat)

custom parts:
  Neopixel Strip -- White (60/m): Neopixel Strip, White, 60 pixels per meter.
